# Fritzing sketch Skema (saved by Fritzing 0.9.3b)

parts:
  Q1 = NPN-Transistor [package="TO92 [THT]"]
  R1 = Resistor [tolerance=±5% resistance=220 package=THT]
  J1 = Piezo Speaker
  U2 = ESP32-38PinWide [part_number=ESP32-38PinWide]
  GPS = SUP500F [package=sup500f]
  Part2 = Adafruit FONA - Mini Cellular GSM Breakout
  Part3 = Tri-Axis Gyro Breakout - L3G4200D

nets:
  GND: Q1.E, U2.GND, GPS.GND, Part2.GND, Part3.GND
  N1: Q1.C, J1.pin1
  N2: R1.Pin_1, U2.GPIO23
  VIN: J1.pin2, U2.VIN, Part3.VCC
  N3: U2.GPIO16, Part2.TXD_5V
  N4: U2.GPIO17, Part2.RXD_5V
  N5: U2.GPIO5, GPS.TX-O
  N6: U2.GPIO21, Part3.SDA
  N7: U2.GPIO22, Part3.SCL
  N8: GPS.VCC, Part2.VCCIO

custom parts:
  ESP32-38PinWide: Generic 38-Pin ESP32 with wide format (only access to one side of pins on a breadboard) based on Stephen Lilley's HiLetgo ESP-WROOM-32 ESP32 ESP-32S Development Board.
  Adafruit FONA - Mini Cellular GSM Breakout: An all-in-one cellular phone module that lets you add voice, text, SMS and GPRS data to your project. Quad-band 850/900/1800/1900MHz - connect onto any global GSM network with any 2G SIM. Includes an onboard LiPoly battery charging circuitry so you can take your project on the go. Also works as an FM radio receiver.
